// Logisim project newss.circ as structural Verilog: 1 circuit, main circuit main
module main (
);

  wire n7447_1_pin1, n7447_1_pin2, n7447_1_pin3, n7447_1_pin6, n7447_1_pin7, n7447_1_pin9, n7447_1_pin10,
       n7447_1_pin11, n7447_1_pin12, n7447_1_pin13, n7447_1_pin14, n7447_1_pin15;

  _7447 u_7447_1 (
    .pin1(n7447_1_pin1), .pin2(n7447_1_pin2), .pin3(n7447_1_pin3), .pin4(n7447_1_pin3), .pin5(n7447_1_pin3),
    .pin6(n7447_1_pin6), .pin7(n7447_1_pin7), .pin15(n7447_1_pin15), .pin14(n7447_1_pin14),
    .pin13(n7447_1_pin13), .pin12(n7447_1_pin12), .pin11(n7447_1_pin11), .pin10(n7447_1_pin10),
    .pin9(n7447_1_pin9));
  _7_Segment_Display u_7_segment_display_1 (
    .g(n7447_1_pin14), .f(n7447_1_pin15), .a(n7447_1_pin13), .b(n7447_1_pin12), .e(n7447_1_pin9),
    .d(n7447_1_pin10), .c(n7447_1_pin11));  // open: dp
  // also tied to VCC on the sheet: n7447_1_pin3

  // Notes on the sheet:
  //   B
  //   C
  //   D
  //   A
endmodule
